# Fritzing sketch motion-sensor-breadboard (saved by Fritzing 0.9.4)
breadboards: 1

parts:
  part = HC-SR501 Body Sensor Module
  Part2 = Adafruit T-Cobbler Plus [part_number="Adafruit #1989 and #2028"]
  R1 = Resistor [tolerance=±5% resistance=220 package=THT]
  LED1 = smd LED [color="Red (633nm)" package="0603 [SMD]"]

nets:
  VCC: part.VCC, Part2.+5V
  N1: part.OUT, Part2.GPIO17
  GND: part.GND, Part2.GND, R1.Pin_0
  N2: Part2.GPIO18, LED1.cathode
  N3: R1.Pin_1, LED1.anode

custom parts:
  HC-SR501 Body Sensor Module: Pyroelectric Infrared PIR Motion Sensor Detector Module
  Adafruit T-Cobbler Plus: The Raspberry Pi has landed on the Maker World like a 40-GPIO pinned, quad-USB ported, credit card sized bomb of DIY joy. And while you can use most of our great Model B accessories by hooking up our downgrade cable, its probably a good time to upgrade your set up and accessorize using all of the 40 pins. That's why we now carry the Assembled Adafruit Pi T-Cobbler Plus - Breakout + Cable for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
