# Fritzing sketch motion-sensor (saved by Fritzing 0.9.4)

parts:
  HC-SR501 = HC-SR501 Body Sensor Module
  Mod1 = Raspberry Pi 4B  # not connected
  Raspberry_Pi_1 = Raspberry Pi 4 [part_number=RPI-4-b]

nets:
  VCC: HC-SR501.VCC, Raspberry_Pi_1.5V
  N1: HC-SR501.OUT, Raspberry_Pi_1.GPIO17
  GND: HC-SR501.GND, Raspberry_Pi_1.GND

custom parts:
  HC-SR501 Body Sensor Module: Pyroelectric Infrared PIR Motion Sensor Detector Module
  Raspberry Pi 4: The RPi4, a faster version of the awesome Raspberry Pi 2 B ARM Board with 40 pin gpio. Ready for special Raspberry Pi B+ and RPi2 Hat (Hardware attached (on) top)
